// Logisim project 4bit cpu.circ as structural Verilog: 3 circuits, main circuit main
module ins_dec (
  input  [4:0] ins,
  input  zero,
  input  carry,
  output sel_src,
  output en_a,
  output en_b,
  output en_r,
  output [2:0] op,
  output str,
  output jmp,
  output hlt
);

  wire and_1_out, and_2_out, and_3_out, and_4_out, decoder_1_out1, decoder_1_out2, decoder_1_out3,
       decoder_1_out4, decoder_1_out5, decoder_1_out6, decoder_1_out7, decoder_1_out8, decoder_1_out9,
       decoder_1_out10, decoder_1_out12, decoder_1_out13, decoder_1_out14, decoder_1_out15, decoder_1_out16;

  Decoder #(.select(5), .disabled(0), .enable("false")) decoder_1 (
    .out1(decoder_1_out1), .out2(decoder_1_out2), .out3(decoder_1_out3), .out4(decoder_1_out4),
    .out5(decoder_1_out5), .out6(decoder_1_out6), .out7(decoder_1_out7), .out8(decoder_1_out8),
    .out9(decoder_1_out9), .out10(decoder_1_out10), .out11(str), .out12(decoder_1_out12),
    .out13(decoder_1_out13), .out14(decoder_1_out14), .out15(decoder_1_out15), .out16(decoder_1_out16),
    .out31(hlt), .sel(ins));  // open: out0, out17, out18, out19, out20, out21, out22, out23, out24, out25, out26, out27, out28, out29, out30
  and and_1 (and_1_out, decoder_1_out13, zero);
  and and_2 (and_2_out, decoder_1_out14, ~zero);  // AND_Gate
  and and_3 (and_3_out, decoder_1_out15, carry);
  and and_4 (and_4_out, decoder_1_out16, ~carry);  // AND_Gate
  or or_1 (sel_src, decoder_1_out3, decoder_1_out4);
  or or_2 (en_a, decoder_1_out1, decoder_1_out3);
  or or_3 (en_b, decoder_1_out2, decoder_1_out4);
  Pull_Resistor pull_resistor_1 (.node(op));
  Priority_Encoder priority_encoder_1 (
    .in0(decoder_1_out5), .in1(decoder_1_out6), .in2(decoder_1_out7), .in3(decoder_1_out8),
    .in4(decoder_1_out9), .in5(decoder_1_out10), .in6(1'b0), .in7(1'b0), .out(op), .gs(en_r));  // open: en_in, en_out
  or or_4 (jmp, decoder_1_out12, and_1_out, and_2_out, and_3_out, and_4_out);
endmodule

module alu (
  input  [3:0] a,
  input  [3:0] b,
  input  [2:0] op,
  output [3:0] r,
  output zero_out,
  output carry_out
);

  wire adder_1_cout, decoder_1_out0, decoder_1_out1, decoder_1_out2, decoder_1_out3, decoder_1_out4,
       decoder_1_out5, subtractor_1_bout;
  wire [3:0] adder_1_out, and_1_out, not_1_out, or_1_out, shifter_1_out, subtractor_1_out;

  Adder #(.width(4)) adder_1 (.a(a), .b(b), .out(adder_1_out), .cout(adder_1_cout));  // open: cin
  Subtractor #(.width(4)) subtractor_1 (.a(a), .b(b), .out(subtractor_1_out), .bout(subtractor_1_bout));  // open: bin
  Shifter #(.width(4)) shifter_1 (.in(a), .\dist (b[1:0]), .out(shifter_1_out));
  assign or_1_out = a | b;  // OR_Gate or_1, 4 bits wide
  assign r = decoder_1_out3 ? or_1_out : 4'bz;  // Controlled_Buffer controlled_buffer_1
  assign r = decoder_1_out4 ? and_1_out : 4'bz;  // Controlled_Buffer controlled_buffer_2
  assign and_1_out = a & b;  // AND_Gate and_1, 4 bits wide
  assign not_1_out = ~a;  // NOT_Gate not_1, 4 bits wide
  assign r = decoder_1_out5 ? not_1_out : 4'bz;  // Controlled_Buffer controlled_buffer_3
  Decoder #(.select(3), .disabled(0), .enable("false")) decoder_1 (
    .out0(decoder_1_out0), .out1(decoder_1_out1), .out2(decoder_1_out2), .out3(decoder_1_out3),
    .out4(decoder_1_out4), .out5(decoder_1_out5), .sel(op));  // open: out6, out7
  assign r = decoder_1_out0 ? adder_1_out : 4'bz;  // Controlled_Buffer controlled_buffer_4
  assign r = decoder_1_out1 ? subtractor_1_out : 4'bz;  // Controlled_Buffer controlled_buffer_5
  assign r = decoder_1_out2 ? shifter_1_out : 4'bz;  // Controlled_Buffer controlled_buffer_6
  nor nor_1 (zero_out, r[0], r[1], r[2], r[3]);
  or or_2 (carry_out, adder_1_cout, subtractor_1_bout);
endmodule

module main (
);

  wire alu_1_carry_out, alu_1_zero_out, and_1_out, Carry_q, clock_1_out, ins_dec_1_en_a, ins_dec_1_en_b,
       ins_dec_1_en_r, ins_dec_1_hlt, ins_dec_1_jmp, ins_dec_1_sel_src, ins_dec_1_str, not_1_out, not_2_out,
       or_1_out, reset_out, Zero_q;
  wire [2:0] ins_dec_1_op;
  wire [3:0] A_q, alu_1_r, B_q, multiplexer_1_out, PC_q, ram_1_data, register_1_q;
  wire [8:0] rom_1_data;

  Button reset (.out(reset_out));
  not not_1 (not_1_out, ins_dec_1_jmp);
  Clock clock_1 (.out(clock_1_out));
  and and_1 (and_1_out, clock_1_out, ~or_1_out);  // AND_Gate
  or or_1 (or_1_out, reset_out, ins_dec_1_hlt);
  Counter #(.width(4), .max('hf)) PC (
    .load(ins_dec_1_jmp), .D(rom_1_data[3:0]), .count(not_1_out), .Q(PC_q), .clk(and_1_out), .clr(reset_out));  // open: carry
  ROM #(.addrWidth(4), .dataWidth(9)) rom_1 (.addr(PC_q), .data(rom_1_data));  // open: sel
  ins_dec ins_dec_1 (
    .ins(rom_1_data[8:4]), .zero(Zero_q), .carry(Carry_q), .sel_src(ins_dec_1_sel_src),
    .en_a(ins_dec_1_en_a), .en_b(ins_dec_1_en_b), .en_r(ins_dec_1_en_r), .op(ins_dec_1_op),
    .str(ins_dec_1_str), .jmp(ins_dec_1_jmp), .hlt(ins_dec_1_hlt));
  not not_2 (not_2_out, ins_dec_1_str);
  RAM #(.addrWidth(4), .dataWidth(4), .bus("separate")) ram_1 (
    .addr(rom_1_data[3:0]), .din(register_1_q), .data(ram_1_data), .str(ins_dec_1_str), .clk(and_1_out),
    .ld(not_2_out));  // open: sel, clr
  Multiplexer #(.width(4), .disabled(0), .enable("false")) multiplexer_1 (
    .in0(ram_1_data), .in1(rom_1_data[3:0]), .out(multiplexer_1_out), .sel(ins_dec_1_sel_src));
  D_Flip_Flop Zero (
    .clk(and_1_out), .D(alu_1_zero_out), .Q(Zero_q), .en(ins_dec_1_en_r), .reset(or_1_out));  // open: Qn, preset
  D_Flip_Flop Carry (
    .clk(and_1_out), .D(alu_1_carry_out), .Q(Carry_q), .en(ins_dec_1_en_r), .reset(or_1_out));  // open: Qn, preset
  Register #(.width(4)) A (.D(multiplexer_1_out), .en(ins_dec_1_en_a), .Q(A_q), .clk(and_1_out), .clr(or_1_out));
  Register #(.width(4)) B (.D(multiplexer_1_out), .en(ins_dec_1_en_b), .Q(B_q), .clk(and_1_out), .clr(or_1_out));
  alu alu_1 (.a(A_q), .b(B_q), .op(ins_dec_1_op), .r(alu_1_r), .zero_out(alu_1_zero_out), .carry_out(alu_1_carry_out));
  Register #(.width(4)) register_1 (
    .D(alu_1_r), .en(ins_dec_1_en_r), .Q(register_1_q), .clk(and_1_out), .clr(or_1_out));
endmodule
