// Logisim project KT8.circ as structural Verilog: 2 circuits, main circuit main
module main (
);

  wire and_1_out, and_2_out, clock_1_out, comparator_1_eq, comparator_1_gt, cpu_1_w_nr, nor_1_out, not_1_out,
       not_2_out;
  wire [3:0] cpu_1_address;
  wire [6:0] bit_extender_2_out, keyboard_1_data;
  wire [7:0] bit_extender_1_out, controlled_buffer_1_out, cpu_1_ram_out;

  cpu cpu_1 (
    .Instruction(controlled_buffer_1_out), .Address(cpu_1_address), .RAM_out(cpu_1_ram_out), .W_nR(cpu_1_w_nr));  // open: RAM_in, Code_address
  Clock clock_1 (.out(clock_1_out));
  Comparator #(.width(4), .mode("unsigned")) comparator_1 (
    .a(cpu_1_address), .b(4'b1110), .gt(comparator_1_gt), .eq(comparator_1_eq));  // open: lt
  nor nor_1 (nor_1_out, comparator_1_gt, comparator_1_eq);
  not not_1 (not_1_out, cpu_1_w_nr);
  Keyboard keyboard_1 (.clk(cpu_1_w_nr), .re(and_1_out), .data(keyboard_1_data));  // open: clr, avail
  not not_2 (not_2_out, nor_1_out);
  and and_1 (and_1_out, not_2_out, ~cpu_1_address[0]);  // AND_Gate
  assign controlled_buffer_1_out = and_1_out ? bit_extender_1_out : 8'bz;  // Controlled_Buffer controlled_buffer_1
  RAM #(.addrWidth(4), .bus("separate")) ram_1 (
    .addr(cpu_1_address), .din(cpu_1_ram_out), .data(controlled_buffer_1_out), .str(cpu_1_w_nr),
    .sel(nor_1_out), .clk(clock_1_out), .ld(not_1_out));  // open: clr
  assign bit_extender_1_out = {{1{1'b0}}, keyboard_1_data};  // Bit_Extender bit_extender_1
  Bit_Extender #(.out_width(7)) bit_extender_2 (.in(cpu_1_ram_out), .out(bit_extender_2_out));
  TTY tty_1 (.data(bit_extender_2_out), .clk(clock_1_out), .we(and_2_out));  // open: clr
  and and_2 (and_2_out, cpu_1_address[0], not_2_out);
endmodule

module cpu (
  input  [7:0] Instruction,
  input  [7:0] RAM_in,
  output Code_address,
  output [3:0] Address,
  output [7:0] RAM_out,
  output W_nR
);

  Pull_Resistor pull_resistor_1 (.node(RAM_out));
  Pull_Resistor pull_resistor_2 (.node(W_nR));
  Pull_Resistor pull_resistor_3 (.node(Code_address));
  Pull_Resistor pull_resistor_4 (.node(Address));
endmodule
